# Fritzing sketch wiring-src (saved by Fritzing 0.9.2b)

parts:
  U1 = ESP8266 WiFi Module [part_number=ESP8266]
  KY-1 = Keyes Relay [package=THT]
  KY-2 = Keyes Relay [package=THT]
  KY-3 = Keyes Relay [package=THT]
  X2 = DB9 Connector [package=db9]
  RHT1 = Humidity and Temperature Sensor RHT03
  R1 = Resistor [tolerance=±5% resistance=4.7k package="1206 [SMD]"]
  R2 = Resistor [tolerance=±5% resistance=10k package=THT]
  X4 = DB9 Connector [package=db9]
  R3 = Resistor [tolerance=±5% resistance=10k package=THT]
  S3 = Round Pushbutton
  U2 = Transformer [package=transformer]
  S4 = Round Pushbutton
  R4 = Resistor [tolerance=±5% resistance=4.7k package="1206 [SMD]"]
  Onderdeel1 = FTDI Basic Programmer
  U3 = V_REG_LD1117VXX [package=78xxl]

nets:
  N1: U1.RXD, X2.8, X2.9
  VCC: U1.VCC, RHT1.Vcc, R1.Pin_1, R2.Pin_0, U3.OUT
  N2: U1.GPIO_0, X2.1
  N3: U1.CH_PD, R2.Pin_1
  GND: U1.GND, U1.GPIO_15, KY-1.ground, KY-2.ground, KY-3.ground, X2.3, X2.4, RHT1.GND_1, RHT1.GND_2, X4.1, R3.Pin_0, U2.4, Onderdeel1.GND
  N4: U1.TXD, X2.6, X2.7
  N5: U1.GPIO_4, RHT1.Data-signal, R1.Pin_0
  N6: U1.GPIO_16, S4.leg0, R4.Pin_0
  N7: U1.GPIO_14, KY-1.signal
  N8: U1.GPIO_12, KY-3.signal
  N9: U1.GPIO_13, KY-2.signal
  N10: KY-1.power, U3.IN
  N11: KY-1.C, KY-3.C, S3.leg0, U2.2
  N12: KY-2.power, U2.1
  N13: KY-2.C, KY-3.NO
  N14: X4.3, R3.Pin_1
  N15: X4.5, X4.6, Onderdeel1.TXO
  N16: X4.7, X4.8, X4.9, Onderdeel1.RXI

notes:
  Parts list:
  - ESP8266-12
  - FTDI-232 (3.3v)
  - DHT22 or AM2302
  - RS232 male conn.
  - RS232 female conn.
  - 3x AC Relay
  - 4.7k Ohm resistors
  - 10k Ohm resistors
  - 5v power supply
  - 3.3v regulator
  - a lot of wires
  SmartStove wiring
  GregNau
  5v
  AC iN
  GND
  3v3
  data
  4,7k
  RELAY #3
  RELAY #2
  CH_PD (EN)
  RELAY #1
  TXD
  RXD
  AM2302
  GPIO0
  RS232
  ESP8266
  REGULATOR
  3V3
  10k
  FLAME
  HIGH
  LOW
  HEATER
  FTDI
  AC-DC 5v
  10µF
  (4-15v)
  DC iN
  DC OUT
  (3.3v)
  3.3v
  MAIN POWER SWITCH
  LOGIC
  *** striped lines are mains electricity, watch out!
  LOGIC BUTTON
  NEUTRAL
  232

custom parts:
  ESP8266 WiFi Module: Generic WiFi Module based on the ESP8266 with onboard PCB antenna and UART communications
  Keyes Relay: The Keyes 5V relay module is suitable for SCM development, home appliance control. It uses a 5V~12V TIL control signal which can control DC / AC signal.
